// Digital circuit Address_Decode.dig as structural Verilog
module Address_Decode (
  input  A1,
  input  A2,
  input  A3,
  input  A4,
  input  A5,
  input  A6,
  input  A7,
  input  A8,
  input  A9,
  input  A10,
  input  A11,
  input  A12,
  input  A0,
  output _0000_0001,
  output nP1EN,
  output _0004_0005,
  output nACIAEN,
  output _0008_0009,
  output nP2EN,
  output nP3EN,
  output nP4EN,
  output _0000_000F,
  output _0010_001F,
  output _0020_002F,
  output _0030_003F,
  output _0040_004F,
  output _0050_005F,
  output _0060_006F,
  output _0070_007F,
  output _0000_007F,
  output _0080_00FF,
  output _0100_017F,
  output _0180_01FF,
  output _0200_027F,
  output _0280_02FF,
  output _0300_037F,
  output _0380_03FF,
  output A0K,
  output A1K,
  output A2K,
  output A3K,
  output A4K,
  output A5K,
  output A6K,
  output A7K,
  output nROMCS,
  output nRAM2CS,
  output nRAMBANK1CS,
  output _0100_010F,
  output _0110_011F,
  output _0120_012F,
  output _0130_013F,
  output _0140_014F,
  output _0150_015F,
  output _0160_016F,
  output _0170_017F,
  output RTCCS1,
  output RTCCS2,
  output nRAM1CS
);

  _74138 _74138_1 (
    .pin1(A1), .pin2(A2), .pin3(A3), .pin4(1'b0), .pin5(_0000_000F), .pin6(1'b1), .pin7(nP4EN), .pin8(1'b0),
    .pin9(nP3EN), .pin10(nP2EN), .pin11(_0008_0009), .pin12(nACIAEN), .pin13(_0004_0005), .pin14(nP1EN),
    .pin15(_0000_0001), .pin16(1'b1));
  _74138 _74138_2 (
    .pin1(A4), .pin2(A5), .pin3(A6), .pin4(1'b0), .pin5(_0000_007F), .pin6(1'b1), .pin7(_0070_007F),
    .pin8(1'b0), .pin9(_0060_006F), .pin10(_0050_005F), .pin11(_0040_004F), .pin12(_0030_003F),
    .pin13(_0020_002F), .pin14(_0010_001F), .pin15(_0000_000F), .pin16(1'b1));
  _74138 _74138_3 (
    .pin1(A7), .pin2(A8), .pin3(A9), .pin4(1'b0), .pin5(A0K), .pin6(1'b1), .pin7(_0380_03FF), .pin8(1'b0),
    .pin9(_0300_037F), .pin10(_0280_02FF), .pin11(_0200_027F), .pin12(_0180_01FF), .pin13(_0100_017F),
    .pin14(_0080_00FF), .pin15(_0000_007F), .pin16(1'b1));
  _74138 _74138_4 (
    .pin1(A10), .pin2(A11), .pin3(A12), .pin4(1'b0), .pin5(1'b0), .pin6(1'b1), .pin7(A7K), .pin8(1'b0),
    .pin9(A6K), .pin10(A5K), .pin11(A4K), .pin12(A3K), .pin13(A2K), .pin14(A1K), .pin15(A0K), .pin16(1'b1));
  and and_1 (nRAMBANK1CS, A0K, A1K);
  and and_2 (nRAM2CS, A2K, A3K);
  and and_3 (nROMCS, A4K, A5K, A6K, A7K);
  _74138 _74138_5 (
    .pin1(A4), .pin2(A5), .pin3(A6), .pin4(1'b0), .pin5(_0100_017F), .pin6(1'b1), .pin7(_0170_017F),
    .pin8(1'b0), .pin9(_0160_016F), .pin10(_0150_015F), .pin11(_0140_014F), .pin12(_0130_013F),
    .pin13(_0120_012F), .pin14(_0110_011F), .pin15(_0100_010F), .pin16(1'b1));
  not not_1 (RTCCS1, _0100_010F);
  nand nand_1 (nRAM1CS, _0100_010F, _0000_007F, ~nRAMBANK1CS);  // NAnd

  assign RTCCS2 = 1'b1;
endmodule

/* Test case ROM ~CS:
A12 A11 A10 ~ROMCS
1   x   x   0
0   x   x   1
*/

/* Test case RAM2 ~CS:
A12 A11 A10 ~RAM2CS
1   x   x   1
0   0   x   1
0   1   x   0
*/

/* Test case RAM1 ~CS:
A12 A11 A10 A9 A8 A7 A6 A5 A4 ~RAM1CS
# 1000 - 1FFF is ROM
1   x   x   x  x  x  x  x  x  1
# 0800 - 0FFF is RAM2
0   1   x   x  x  x  x  x  x  1
# 0000 - 07FF is RAM1, with exceptions
0   0   1   x  x  x  x  x  x  0
0   0   0   1  x  x  x  x  x  0
0   0   0   0  1  1  x  x  x  0
0   0   0   0  1  0  1  x  x  0
0   0   0   0  1  0  0  1  x  0
0   0   0   0  1  0  0  0  1  0
# 0100 - 010F is RTC
0   0   0   0  1  0  0  0  0  1
# 80 - FF is external RAM
0   0   0   0  0  1  x  x  x  0
# 00 - 7F is internal RAM
0   0   0   0  0  0  x  x  x  1
*/

/* Test case RTC CS1:
A12 A11 A10 A9 A8 A7 A6 A5 A4 RTCCS1
1   x   x   x  x  x  x  x  x  0
0   1   x   x  x  x  x  x  x  0
0   0   1   x  x  x  x  x  x  0
0   0   0   1  x  x  x  x  1  0
0   0   0   0  1  1  x  x  x  0
0   0   0   0  1  0  1  x  x  0
0   0   0   0  1  0  0  1  x  0
0   0   0   0  1  0  0  0  0  1
0   0   0   0  0  1  x  x  x  0
0   0   0   0  0  0  1  x  x  0
0   0   0   0  0  0  0  1  x  0
*/

/* Test case Pair 1 ~EN:
A12 A11 A10 A9 A8 A7 A6 A5 A4 A3 A2 A1 ~P1EN
0   0   0   0  0  0  0  0  0  0  0  0  1
0   0   0   0  0  0  0  0  0  0  0  1  0
0   0   0   0  0  0  0  0  0  0  1  0  1
0   0   0   0  0  0  0  0  0  0  1  1  1
0   0   0   0  0  0  0  0  0  1  0  0  1
0   0   0   0  0  0  0  0  0  1  0  1  1
0   0   0   0  0  0  0  0  0  1  1  0  1
0   0   0   0  0  0  0  0  0  1  1  1  1
x   x   x   x  x  x  x  x  1  x  x  x  1
x   x   x   x  x  x  x  1  0  x  x  x  1
x   x   x   x  x  x  1  0  0  x  x  x  1
x   x   x   x  x  1  0  0  0  x  x  x  1
x   x   x   x  1  0  0  0  0  x  x  x  1
x   x   x   1  0  0  0  0  0  x  x  x  1
x   x   1   0  0  0  0  0  0  x  x  x  1
x   1   0   0  0  0  0  0  0  x  x  x  1
1   0   0   0  0  0  0  0  0  x  x  x  1
*/

/* Test case ACIA ~EN:
A12 A11 A10 A9 A8 A7 A6 A5 A4 A3 A2 A1 ~ACIAEN
0   0   0   0  0  0  0  0  0  0  0  0  1
0   0   0   0  0  0  0  0  0  0  0  1  1
0   0   0   0  0  0  0  0  0  0  1  0  1
0   0   0   0  0  0  0  0  0  0  1  1  0
0   0   0   0  0  0  0  0  0  1  0  0  1
0   0   0   0  0  0  0  0  0  1  0  1  1
0   0   0   0  0  0  0  0  0  1  1  0  1
0   0   0   0  0  0  0  0  0  1  1  1  1
x   x   x   x  x  x  x  x  1  x  x  x  1
x   x   x   x  x  x  x  1  0  x  x  x  1
x   x   x   x  x  x  1  0  0  x  x  x  1
x   x   x   x  x  1  0  0  0  x  x  x  1
x   x   x   x  1  0  0  0  0  x  x  x  1
x   x   x   1  0  0  0  0  0  x  x  x  1
x   x   1   0  0  0  0  0  0  x  x  x  1
x   1   0   0  0  0  0  0  0  x  x  x  1
1   0   0   0  0  0  0  0  0  x  x  x  1
*/

/* Test case Pair 2 ~EN:
A12 A11 A10 A9 A8 A7 A6 A5 A4 A3 A2 A1 ~P2EN
0   0   0   0  0  0  0  0  0  0  0  0  1
0   0   0   0  0  0  0  0  0  0  0  1  1
0   0   0   0  0  0  0  0  0  0  1  0  1
0   0   0   0  0  0  0  0  0  0  1  1  1
0   0   0   0  0  0  0  0  0  1  0  0  1
0   0   0   0  0  0  0  0  0  1  0  1  0
0   0   0   0  0  0  0  0  0  1  1  0  1
0   0   0   0  0  0  0  0  0  1  1  1  1
x   x   x   x  x  x  x  x  1  x  x  x  1
x   x   x   x  x  x  x  1  0  x  x  x  1
x   x   x   x  x  x  1  0  0  x  x  x  1
x   x   x   x  x  1  0  0  0  x  x  x  1
x   x   x   x  1  0  0  0  0  x  x  x  1
x   x   x   1  0  0  0  0  0  x  x  x  1
x   x   1   0  0  0  0  0  0  x  x  x  1
x   1   0   0  0  0  0  0  0  x  x  x  1
1   0   0   0  0  0  0  0  0  x  x  x  1
*/

/* Test case Pair 3 ~EN:
A12 A11 A10 A9 A8 A7 A6 A5 A4 A3 A2 A1 ~P3EN
0   0   0   0  0  0  0  0  0  0  0  0  1
0   0   0   0  0  0  0  0  0  0  0  1  1
0   0   0   0  0  0  0  0  0  0  1  0  1
0   0   0   0  0  0  0  0  0  0  1  1  1
0   0   0   0  0  0  0  0  0  1  0  0  1
0   0   0   0  0  0  0  0  0  1  0  1  1
0   0   0   0  0  0  0  0  0  1  1  0  0
0   0   0   0  0  0  0  0  0  1  1  1  1
x   x   x   x  x  x  x  x  1  x  x  x  1
x   x   x   x  x  x  x  1  0  x  x  x  1
x   x   x   x  x  x  1  0  0  x  x  x  1
x   x   x   x  x  1  0  0  0  x  x  x  1
x   x   x   x  1  0  0  0  0  x  x  x  1
x   x   x   1  0  0  0  0  0  x  x  x  1
x   x   1   0  0  0  0  0  0  x  x  x  1
x   1   0   0  0  0  0  0  0  x  x  x  1
1   0   0   0  0  0  0  0  0  x  x  x  1
*/

/* Test case Pair 4 ~EN:
A12 A11 A10 A9 A8 A7 A6 A5 A4 A3 A2 A1 ~P4EN
0   0   0   0  0  0  0  0  0  0  0  0  1
0   0   0   0  0  0  0  0  0  0  0  1  1
0   0   0   0  0  0  0  0  0  0  1  0  1
0   0   0   0  0  0  0  0  0  0  1  1  1
0   0   0   0  0  0  0  0  0  1  0  0  1
0   0   0   0  0  0  0  0  0  1  0  1  1
0   0   0   0  0  0  0  0  0  1  1  0  1
0   0   0   0  0  0  0  0  0  1  1  1  0
x   x   x   x  x  x  x  x  1  x  x  x  1
x   x   x   x  x  x  x  1  0  x  x  x  1
x   x   x   x  x  x  1  0  0  x  x  x  1
x   x   x   x  x  1  0  0  0  x  x  x  1
x   x   x   x  1  0  0  0  0  x  x  x  1
x   x   x   1  0  0  0  0  0  x  x  x  1
x   x   1   0  0  0  0  0  0  x  x  x  1
x   1   0   0  0  0  0  0  0  x  x  x  1
1   0   0   0  0  0  0  0  0  x  x  x  1
*/
