// Digital circuit Address_Latch.dig as structural Verilog
module Address_Latch (
  input  PB0,
  input  PB1,
  input  PB2,
  input  PB3,
  input  PB4,
  input  PB5,
  input  PB6,
  input  PB7,
  input  AS,
  output A0,
  output A1,
  output A2,
  output A3,
  output A4,
  output A5,
  output A6,
  output A7
);

  _74373 _74373_1 (
    .pin1(1'b0), .pin2(A0), .pin3(PB0), .pin4(PB1), .pin5(A1), .pin6(A2), .pin7(PB2), .pin8(PB3), .pin9(A3),
    .pin10(1'b0), .pin11(AS), .pin12(A4), .pin13(PB4), .pin14(PB5), .pin15(A5), .pin16(A6), .pin17(PB6),
    .pin18(PB7), .pin19(A7), .pin20(1'b1));
endmodule

/* Test case A0-A7 Latch:
AS PB0 PB1 PB2 PB3 PB4 PB5 PB6 PB7 A0 A1 A2 A3 A4 A5 A6 A7
0  0   0   0   0   0   0   0   0   0  0  0  0  0  0  0  0
C  1   1   1   1   1   1   1   1   1  1  1  1  1  1  1  1
C  1   0   1   0   1   0   1   0   1  0  1  0  1  0  1  0
C  0   1   0   1   0   1   0   1   0  1  0  1  0  1  0  1
*/
