// Digital circuit New_Address_Decode.dig as structural Verilog
module New_Address_Decode (
  input  A0,
  input  A1,
  input  A2,
  input  A3,
  input  A4,
  input  A5,
  input  A6,
  input  A7,
  input  A8,
  input  A9,
  input  A10,
  input  A11,
  input  A12,
  input  R_nW,
  input  AS,
  output nRAM2CS,
  output nQ4,
  output nQ5,
  output nQ6,
  output nQ7,
  output nROMCS,
  output RTCCS,
  output nRAM1CS,
  output _0000_0001,
  output nP1EN,
  output _0004_0005,
  output nACIAEN,
  output n1Q40006_0007,
  output nP2EN,
  output nP3EN,
  output nP4EN
);

  wire and_1_out, and_2_out, and_3_out, and_4_out, and_5_out, MX1_pin12, MX1_pin13, MX1_pin15, MX2_pin7,
       MX2_pin9, MX2_pin10, MX2_pin11, MX2_pin12, MX2_pin13, MX2_pin14, MX2_pin15, or_1_out, or_2_out,
       or_3_out;

  _74138 MX1 (
    .pin1(A11), .pin2(A12), .pin3(1'b0), .pin4(1'b0), .pin5(1'b0), .pin6(AS), .pin7(nQ7), .pin8(1'b0),
    .pin9(nQ6), .pin10(nQ5), .pin11(nQ4), .pin12(MX1_pin12), .pin13(MX1_pin13), .pin14(nRAM2CS),
    .pin15(MX1_pin15), .pin16(1'b1));
  or or_1 (or_1_out, A4, A5, A6, A7);
  and and_1 (and_1_out, ~A7, ~A6, ~A5, ~A4);  // And
  _74138 MX2 (
    .pin1(A8), .pin2(A9), .pin3(A10), .pin4(MX1_pin15), .pin5(MX1_pin15), .pin6(AS), .pin7(MX2_pin7),
    .pin8(1'b0), .pin9(MX2_pin9), .pin10(MX2_pin10), .pin11(MX2_pin11), .pin12(MX2_pin12), .pin13(MX2_pin13),
    .pin14(MX2_pin14), .pin15(MX2_pin15), .pin16(1'b1));
  and and_2 (and_2_out, ~A7, ~A8);  // And
  nor nor_1 (RTCCS, or_1_out, MX2_pin14);
  and and_3 (and_3_out, MX2_pin15, MX2_pin14);
  or or_2 (or_2_out, or_1_out, MX2_pin15);
  and and_4 (and_4_out, MX2_pin13, MX2_pin12, MX2_pin11);
  and and_5 (and_5_out, MX2_pin10, MX2_pin9, MX2_pin7);
  or or_3 (or_3_out, and_1_out, and_2_out, and_3_out);
  and and_6 (nRAM1CS, or_3_out, and_4_out, and_5_out);
  _74138 MX3 (
    .pin1(A1), .pin2(A2), .pin3(A3), .pin4(or_2_out), .pin5(or_2_out), .pin6(AS), .pin7(nP4EN), .pin8(1'b0),
    .pin9(nP3EN), .pin10(nP2EN), .pin11(n1Q40006_0007), .pin12(nACIAEN), .pin13(_0004_0005), .pin14(nP1EN),
    .pin15(_0000_0001), .pin16(1'b1));
  and and_7 (nROMCS, MX1_pin13, MX1_pin12);

  // Notes on the sheet:
  //   R_nW: Read High, Write Low
  //   AS: Address Select
  //   nRAM2CS: RAM 2 ~CE
  //   nQ4: Unused
  //   nQ5: Unused
  //   nQ6: Unused
  //   nQ7: Unused
  //   _0000_0001: Unused
  //   _0004_0005: Unused
  //   n1Q40006_0007: Unused
endmodule

/* Test case ROM ~CS:
AS A12 A11 A10 A9 A8 A7 A6 A5 A4 A3 A2 A1 A0 ~ROMCS
0   X   X   X   X  X  X  X  X  X  X  X  X  X    1
1   1   X   X   X  X  X  X  X  X  X  X  X  X    0
1   0   X   X   X  X  X  X  X  X  X  X  X  X    1
*/

/* Test case RAM 2 ~CS:
AS A12 A11 A10 A9 A8 A7 A6 A5 A4 A3 A2 A1 A0 ~RAM2CS
0   X   X   X   X  X  X  X  X  X  X  X  X  X    1
1   1   X   X   X  X  X  X  X  X  X  X  X  X    1
1   0   1   X   X  X  X  X  X  X  X  X  X  X    0
1   0   0   X   X  X  X  X  X  X  X  X  X  X    1
*/

/* Test case RTC CS:
AS A12 A11 A10 A9 A8 A7 A6 A5 A4 A3 A2 A1 A0 RTCCS
0   X   X   X   X  X  X  X  X  X  X  X  X  X   0
1   1   X   X   X  X  X  X  X  X  X  X  X  X   0
1   0   1   X   X  X  X  X  X  X  X  X  X  X   0
1   0   0   1   X  X  X  X  X  X  X  X  X  X   0
1   0   0   0   1  X  X  X  X  X  X  X  X  X   0
1   0   0   0   0  1  1  X  X  X  X  X  X  X   0
1   0   0   0   0  1  0  1  X  X  X  X  X  X   0
1   0   0   0   0  1  0  0  1  X  X  X  X  X   0
1   0   0   0   0  1  0  0  0  1  X  X  X  X   0
1   0   0   0   0  1  0  0  0  0  X  X  X  X   1
1   X   X   X   X  0  X  X  X  X  X  X  X  X   0
*/

/* Test case RAM 1 ~CS:
AS A12 A11 A10 A9 A8 A7 A6 A5 A4 A3 A2 A1 A0 ~RAM1CS
0   X   X   X   X  X  X  X  X  X  X  X  X  X    1
# 1000 - 1FFF is ROM
1   1   X   X   X  X  X  X  X  X  X  X  X  X    1
# 0800 - 0FFF is RAM2
1   0   1   X   X  X  X  X  X  X  X  X  X  X    1
# 0000 - 07FF is RAM1, with exceptions
1   0   0   1   X  X  X  X  X  X  X  X  X  X    0
1   0   0   0   1  X  X  X  X  X  X  X  X  X    0
1   0   0   0   0  1  1  X  X  X  X  X  X  X    0
1   0   0   0   0  1  0  1  X  X  X  X  X  X    0
1   0   0   0   0  1  0  0  1  X  X  X  X  X    0
1   0   0   0   0  1  0  0  0  1  X  X  X  X    0
# 0100 - 010F is RTC
1   0   0   0   0  1  0  0  0  0  X  X  X  X    1
# 80 - FF is external RAM
1   0   0   0   0  0  1  X  X  X  X  X  X  X    0
# 00 - 7F is internal RAM
1   0   0   0   0  0  0  X  X  X  X  X  X  X    1
*/

/* Test case ORG RTC CS:
AS A12 A11 A10 A9 A8 A7 A6 A5 A4 RTCCS
1   1   x   x   x  x  x  x  x  x  0
1   0   1   x   x  x  x  x  x  x  0
1   0   0   1   x  x  x  x  x  x  0
1   0   0   0   1  x  x  x  x  1  0
1   0   0   0   0  1  1  x  x  x  0
1   0   0   0   0  1  0  1  x  x  0
1   0   0   0   0  1  0  0  1  x  0
1   0   0   0   0  1  0  0  0  0  1
1   0   0   0   0  0  1  x  x  x  0
1   0   0   0   0  0  0  1  x  x  0
1   0   0   0   0  0  0  0  1  x  0
*/

/* Test case Pair 1 ~EN:
AS A12 A11 A10 A9 A8 A7 A6 A5 A4 A3 A2 A1 A0 ~P1EN
0   x   x   x   x  x  x  x  x  x  x  x  x  x  1
1   0   0   0   0  0  0  0  0  0  0  0  0  x  1
1   0   0   0   0  0  0  0  0  0  0  0  1  x  0

1   0   0   0   0  0  0  0  0  0  0  1  0  x  1
1   0   0   0   0  0  0  0  0  0  0  1  1  x  1
1   0   0   0   0  0  0  0  0  0  1  0  0  x  1
1   0   0   0   0  0  0  0  0  0  1  0  1  x  1
1   0   0   0   0  0  0  0  0  0  1  1  0  x  1
1   0   0   0   0  0  0  0  0  0  1  1  1  x  1
1   x   x   x   x  x  x  x  x  1  x  x  x  x  1
1   x   x   x   x  x  x  x  1  0  x  x  x  x  1
1   x   x   x   x  x  x  1  0  0  x  x  x  x  1
1   x   x   x   x  x  1  0  0  0  x  x  x  x  1
1   x   x   x   x  1  0  0  0  0  x  x  x  x  1
1   x   x   x   1  0  0  0  0  0  x  x  x  x  1
1   x   x   1   0  0  0  0  0  0  x  x  x  x  1
1   x   1   0   0  0  0  0  0  0  x  x  x  x  1
1   1   0   0   0  0  0  0  0  0  x  x  x  x  1
*/

/* Test case ACIA ~EN:
AS A12 A11 A10 A9 A8 A7 A6 A5 A4 A3 A2 A1 A0 ~ACIAEN
0   x   x   x   x  x  x  x  x  x  x  x  x  x  1  
1   0   0   0   0  0  0  0  0  0  0  0  0  x  1
1   0   0   0   0  0  0  0  0  0  0  0  1  x  1
1   0   0   0   0  0  0  0  0  0  0  1  0  x  1
1   0   0   0   0  0  0  0  0  0  0  1  1  x  0
1   0   0   0   0  0  0  0  0  0  1  0  0  x  1
1   0   0   0   0  0  0  0  0  0  1  0  1  x  1
1   0   0   0   0  0  0  0  0  0  1  1  0  x  1
1   0   0   0   0  0  0  0  0  0  1  1  1  x  1
1   x   x   x   x  x  x  x  x  1  x  x  x  x  1
1   x   x   x   x  x  x  x  1  0  x  x  x  x  1
1   x   x   x   x  x  x  1  0  0  x  x  x  x  1
1   x   x   x   x  x  1  0  0  0  x  x  x  x  1
1   x   x   x   x  1  0  0  0  0  x  x  x  x  1
1   x   x   x   1  0  0  0  0  0  x  x  x  x  1
1   x   x   1   0  0  0  0  0  0  x  x  x  x  1
1   x   1   0   0  0  0  0  0  0  x  x  x  x  1
1   1   0   0   0  0  0  0  0  0  x  x  x  x  1
*/

/* Test case Pair 2 ~EN:
AS A12 A11 A10 A9 A8 A7 A6 A5 A4 A3 A2 A1 A0 ~P2EN
0  x   x   x   x  x  x  x  x  x  x  x  x  x  1    
1  0   0   0   0  0  0  0  0  0  0  0  0  x  1
1  0   0   0   0  0  0  0  0  0  0  0  1  x  1
1  0   0   0   0  0  0  0  0  0  0  1  0  x  1
1  0   0   0   0  0  0  0  0  0  0  1  1  x  1
1  0   0   0   0  0  0  0  0  0  1  0  0  x  1
1  0   0   0   0  0  0  0  0  0  1  0  1  x  0
1  0   0   0   0  0  0  0  0  0  1  1  0  x  1
1  0   0   0   0  0  0  0  0  0  1  1  1  x  1
1  x   x   x   x  x  x  x  x  1  x  x  x  x  1
1  x   x   x   x  x  x  x  1  0  x  x  x  x  1
1  x   x   x   x  x  x  1  0  0  x  x  x  x  1
1  x   x   x   x  x  1  0  0  0  x  x  x  x  1
1  x   x   x   x  1  0  0  0  0  x  x  x  x  1
1  x   x   x   1  0  0  0  0  0  x  x  x  x  1
1  x   x   1   0  0  0  0  0  0  x  x  x  x  1
1  x   1   0   0  0  0  0  0  0  x  x  x  x  1
1  1   0   0   0  0  0  0  0  0  x  x  x  x  1
*/

/* Test case Pair 3 ~EN:
AS A12 A11 A10 A9 A8 A7 A6 A5 A4 A3 A2 A1 A0 ~P3EN
0  x   x   x   x  x  x  x  x  x  x  x  x  x  1    
1  0   0   0   0  0  0  0  0  0  0  0  0  x  1
1  0   0   0   0  0  0  0  0  0  0  0  1  x  1
1  0   0   0   0  0  0  0  0  0  0  1  0  x  1
1  0   0   0   0  0  0  0  0  0  0  1  1  x  1
1  0   0   0   0  0  0  0  0  0  1  0  0  x  1
1  0   0   0   0  0  0  0  0  0  1  0  1  x  1
1  0   0   0   0  0  0  0  0  0  1  1  0  x  0
1  0   0   0   0  0  0  0  0  0  1  1  1  x  1
1  x   x   x   x  x  x  x  x  1  x  x  x  x  1
1  x   x   x   x  x  x  x  1  0  x  x  x  x  1
1  x   x   x   x  x  x  1  0  0  x  x  x  x  1
1  x   x   x   x  x  1  0  0  0  x  x  x  x  1
1  x   x   x   x  1  0  0  0  0  x  x  x  x  1
1  x   x   x   1  0  0  0  0  0  x  x  x  x  1
1  x   x   1   0  0  0  0  0  0  x  x  x  x  1
1  x   1   0   0  0  0  0  0  0  x  x  x  x  1
1  1   0   0   0  0  0  0  0  0  x  x  x  x  1
*/

/* Test case Pair 4 ~EN:
AS A12 A11 A10 A9 A8 A7 A6 A5 A4 A3 A2 A1 A0 ~P4EN
0  x   x   x   x  x  x  x  x  x  x  x  x  x  1    
1  0   0   0   0  0  0  0  0  0  0  0  0  x  1
1  0   0   0   0  0  0  0  0  0  0  0  1  x  1
1  0   0   0   0  0  0  0  0  0  0  1  0  x  1
1  0   0   0   0  0  0  0  0  0  0  1  1  x  1
1  0   0   0   0  0  0  0  0  0  1  0  0  x  1
1  0   0   0   0  0  0  0  0  0  1  0  1  x  1
1  0   0   0   0  0  0  0  0  0  1  1  0  x  1
1  0   0   0   0  0  0  0  0  0  1  1  1  x  0
1  x   x   x   x  x  x  x  x  1  x  x  x  x  1
1  x   x   x   x  x  x  x  1  0  x  x  x  x  1
1  x   x   x   x  x  x  1  0  0  x  x  x  x  1
1  x   x   x   x  x  1  0  0  0  x  x  x  x  1
1  x   x   x   x  1  0  0  0  0  x  x  x  x  1
1  x   x   x   1  0  0  0  0  0  x  x  x  x  1
1  x   x   1   0  0  0  0  0  0  x  x  x  x  1
1  x   1   0   0  0  0  0  0  0  x  x  x  x  1
1  1   0   0   0  0  0  0  0  0  x  x  x  x  1
*/
